# Fritzing sketch Circuit (saved by Fritzing 0.9.3b)
breadboards: 1

parts:
  U1 = NodeMCU V1.0
  VCC1 = Battery block 9V
  IC1 = Voltage Regulator [package=78xxl]
  hc-sr1 = hc-sr04

nets:
  GND: U1.GND, VCC1.-, IC1.GND, hc-sr1.GND
  N1: U1.D5, hc-sr1.Echo
  N2: U1.D6, hc-sr1.Trig
  VIN: U1.Vin, IC1.OUT, hc-sr1.VCC
  N3: VCC1.+, IC1.IN

custom parts:
  NodeMCU V1.0: ESP8266 based NodeMCU
