# Fritzing sketch pulldown (saved by Fritzing 0.9.3b)
breadboards: 1

parts:
  R1 = Resistor [tolerance=±5% resistance=1k package=THT]
  Part1 = Arduino Uno (Rev3)
  S1 = Pushbutton [package="[THT]"]

nets:
  N1: R1.Pin_0, Part1.A0, Part1.D2, S1.Pin_1, S1.Pin_2
  N2: R1.Pin_1, Part1.GND
  N3: Part1.5V, S1.Pin_3, S1.Pin_4
